# Fritzing sketch circuit (saved by Fritzing 0.9.3b)

parts:
  Part1 = Arduino Uno (Rev3)
  SONAR1 = Maxbotix MaxSonar Ultrasonic Sensor
  hc-sr1 = hc-sr04
  U1 = SWITCH-SPST-2 [package=switch-spst-vertical]

nets:
  N1: Part1.A0, SONAR1.AN
  N2: Part1.D13/SCK, U1.P
  GND: Part1.GND, SONAR1.GND, U1.O
  N3: Part1.D2, SONAR1.TX
  N4: Part1.D4, SONAR1.RX
  N5: Part1.D5_PWM, SONAR1.PW
  N6: Part1.D6_PWM, hc-sr1.Echo
  N7: Part1.D7, hc-sr1.Trig
  5V: Part1.5V, SONAR1.+5V

notes:
  MaxSonar-EZ
  1-BW-
  open/low: serial on TX
  high: TX sends pulse for chaining
  2-PW- pulse width @ 147uS per inch
  3-AN- Vcc/512 per inch corresponding to last range
  4-RX–
  open/high: continuous
  low-high-low: >20uS to trigger reading
  5-TX-
  BW low: serial @ 9600-8,n,1 data="Rxxx/r” (0-255 in)
  BW high: chaining trigger pulse
  HC-SR04 Enable

custom parts:
  Maxbotix MaxSonar Ultrasonic Sensor: Maxbotix MaxSonar Ultrasonic Sensor LV-EZ0, LV-EZ1, LV-EZ2, LV-EZ3, LV-EZ4
