# Fritzing sketch circuit (saved by Fritzing 0.9.3b)

parts:
  Part1 = Arduino Uno (Rev3)
  JP2 = Header 8 [package=bm08b-srss-tb]

nets:
  N1: Part1.A0, JP2.3
  N2: Part1.D3_PWM, JP2.2
  N3: Part1.5V, JP2.6
  N4: Part1.GND, JP2.7

notes:
  LV-MaxSonar-EZ
